# Fritzing sketch arduinoStrip (saved by Fritzing 0.8.0b)

parts:
  Teensy_3_1 = Teensy 3.0
  LED1 = RGB LED (com. anode, rbg) [package="5 mm [THT]"]
  BAT1 = Battery Holders [package=battcon_12mm_pth]  # not connected
  VCC1 = 4 x AAA Battery Mount  # not connected
  BAT2 = Battery Holders [package=battcon_12mm]  # not connected

nets (from the breadboard view):
  N1: Teensy_3_1.GND, LED1.green_cathode
  N2: Teensy_3_1.D2, LED1.blue_cathode
  N3: Teensy_3_1.D3, LED1.common_anode
  N4: Teensy_3_1.Vin, LED1.red_cathode
