# Fritzing sketch trimpot-ir-led-button (saved by Fritzing 0.7.11b)
breadboards: 1

parts:
  Arduino_Leonardo = Arduino
  LED2 = LED - 5mm [color="Infrared (940nm)" package="5 mm [THT]"]
  LED1 = LED - 5mm [color="White (6500K)" package="5 mm [THT]"]
  IR1 = TSOP312.., 314.. [package=THT]
  S1 = Pushbutton [package="[THT]"]
  R1 = Trimmer Potentiometer [maximum_resistance=10kΩ package=THT]

nets (from the schematic view):
  GND: Arduino_Leonardo.GND, LED2.cathode, LED1.cathode, IR1.GND, S1.Pin_3, S1.Pin_4, R1.leg2
  N1: Arduino_Leonardo.D11, IR1.Data
  N2: Arduino_Leonardo.D9, LED1.anode
  N3: Arduino_Leonardo.D3, LED2.anode
  N4: Arduino_Leonardo.D2, S1.Pin_1, S1.Pin_2
  N5: Arduino_Leonardo.+5V, IR1.Vs, R1.leg1
  N6: Arduino_Leonardo.A0, R1.wiper
